// Digital circuit Processor.dig as structural Verilog
// Einfacher Prozessor, der an die MIPS-Architektur 
// angelehnt ist. Es handelt sich um eine Harvard 
// Single-Cycle CPU.
module Processor (
  input  Clock
);

  wire abs, ALU2D, alu_1_carry, alu_1_neg, alu_1_zero, branch_1_jmp, flags_1_co, flags_1_no, flags_1_zo, imm,
       ioR, ioW, ld, muxA, sf, src2D, st, stPC, WE;
  wire [2:0] br, muxB;
  wire [4:0] ALUop;
  wire [15:0] alu_1_y, driver_1_out, imreg_1_imm, multiplexer_1_out, multiplexer_2_out, pc_1_next, pc_1_pc,
       register_1_rdest, register_1_rsrc, rom_1_d, signext_1__5d, signext_1__5s, signext_1__9sd;

  PC pc_1 (.ALU(alu_1_y), .C(Clock), .abs(abs), .rel(branch_1_jmp), .Next(pc_1_next), .PC(pc_1_pc));
  ROM #(.isProgramMemory("true"), .Bits(16), .Addr_Bits(16)) rom_1 (.A(pc_1_pc), .sel(1'b1), .D(rom_1_d));
  PullDown #(.Bits(16)) pulldown_1 (.out(rom_1_d));
  assign driver_1_out = stPC ? pc_1_next : 16'bz;  // Driver driver_1
  Control control_1 (
    .Op(rom_1_d[15:9]), .stPC(stPC), .WE(WE), .imm(imm), .absJmp(abs), .muxB(muxB), .srcToD(src2D),
    .muxA(muxA), .ALUToBus(ALU2D), .ALUop(ALUop), .storeFlags(sf), .Branch(br), .st(st), .ld(ld), .ioW(ioW),
    .ioR(ioR));
  Register register_1 (
    .WD(driver_1_out), .C(Clock), .src(rom_1_d[3:0]), .dest(rom_1_d[7:4]), .WE(WE), .Rdest(register_1_rdest),
    .Rsrc(register_1_rsrc));
  ImReg imreg_1 (.inst(rom_1_d), .en(imm), .C(Clock), .imm(imreg_1_imm));
  SignExt signext_1 (.inst(rom_1_d), ._5S(signext_1__5s), ._9SD(signext_1__9sd), ._5D(signext_1__5d));
  assign driver_1_out = src2D ? register_1_rsrc : 16'bz;  // Driver driver_2
  Multiplexer #(.Bits(16)) multiplexer_1 (
    .sel(muxA), .in_0(register_1_rdest), .in_1(register_1_rsrc), .out(multiplexer_1_out));
  Multiplexer #(.Selector_Bits(3), .Bits(16)) multiplexer_2 (
    .sel(muxB), .in_0(register_1_rsrc), .in_1(imreg_1_imm), .in_2({16{1'b0}}), .in_3(16'hff), .in_4(16'hfff),
    .in_5(signext_1__5s), .in_6(signext_1__9sd), .in_7(signext_1__5d), .out(multiplexer_2_out));
  Branch branch_1 (.Z(flags_1_zo), .N(flags_1_no), .C(flags_1_co), .ctrl(br), .jmp(branch_1_jmp));
  ALU alu_1 (
    .A(multiplexer_1_out), .B(multiplexer_2_out), .Op(ALUop), .Ci(flags_1_co), .Y(alu_1_y),
    .Zero(alu_1_zero), .Neg(alu_1_neg), .Carry(alu_1_carry));
  Flags flags_1 (
    .Zi(alu_1_zero), .Ni(alu_1_neg), .Ci(alu_1_carry), .C(Clock), .store(sf), .Zo(flags_1_zo),
    .No(flags_1_no), .Co(flags_1_co));
  assign driver_1_out = ALU2D ? alu_1_y : 16'bz;  // Driver driver_3
  RAMSinglePort #(.Bits(16), .Addr_Bits(16)) ramsingleport_1 (
    .A(alu_1_y), .str(st), .C(Clock), .ld(ld), .D(driver_1_out));
  Graphics graphics_1 (.A(alu_1_y), .R(ioR), .C(Clock), .W(ioW), .D(driver_1_out));

  // Other names for the same wires on the sheet: C = Clock

  // Notes on the sheet:
  //   Clock: Hz: 500000
  //   contents of rom_1 (hex, n*v repeats v):
  //   105
  //   32768
  //   4960
  //   33168
  //   4944
  //   5264
  //   5251
  //   5157
  //   5178
  //   8417
  //   5372
  //   19695
  //   28245
  //   6177
  //   15407
  //   26105
  //   28190
  //   517
  //   534
  //   5168
  //   5152
  //   5280
  //   32819
  //   26816
  //   31360
  //   15488
  //   24069
  //   15474
  //   24069
  //   15475
  //   24067
  //   28163
  //   15475
  //   25601
  //   5283
  //   29722
  //   6145
  //   6161
  //   6177
  //   15652
  //   26092
  //   6193
  //   15668
  //   26088
  //   12433
  //   65535
  //   28681
  //   582
  //   613
  //   596
  //   31744
  //   28637
  //   5232
  //   8241
  //   8452
  //   32856
  //   26800
  //   6177
  //   6145
  //   32856
  //   26800
  //   6193
  //   6404
  //   32856
  //   26800
  //   6193
  //   6404
  //   32856
  //   26800
  //   8225
  //   8193
  //   32856
  //   26800
  //   8225
  //   8193
  //   32856
  //   26800
  //   8241
  //   8452
  //   32856
  //   26800
  //   8241
  //   8452
  //   32856
  //   26800
  //   6177
  //   6193
  //   6405
  //   27148
  //   15652
  //   25094
  //   15668
  //   25092
  //   31360
  //   15488
  //   24065
  //   6257
  //   27147
  //   579
  //   14148
  //   1090
  //   1094
  //   29768
  //   20222
  //   6369
  //   27151
endmodule
