// Digital circuit ProcessorIntr.dig as structural Verilog
// Simple processor based on the MIPS architecture. 
// It is a Harvard single-cycle CPU.
// {{de Einfacher Prozessor, der an die MIPS-Architektur 
// angelehnt ist. Es handelt sich um eine Harvard 
// Single-Cycle CPU.}}
module ProcessorIntr (
  input  C,
  input  intr,
  output [15:0] D,
  output [15:0] A,
  output ioR,
  output ioW
);

  wire abs, alu2D, alu_1_p6, alu_1_p7, alu_1_p8, aluOp, br, branch_1_p3, branch_1_p4, branch_1_p5,
       flagsrw_1_p1, iem, imm, intr_t, ld, muxA, pcintr_1_p6, RetI, sf, src2D, st, stPC, WE;
  wire [2:0] muxB;
  wire [3:0] rom_1_d, rom_1_d_2;
  wire [7:0] rom_1_d_3;
  wire [15:0] imreg_1_p5, multiplexer_1_out, multiplexer_2_out, pcintr_1_p7, pcintr_1_p8, register_1_p6,
       register_1_p7, signext_1_p2, signext_1_p3, signext_1_p4;

  ROM #(.AddrBits(16), .isProgramMemory("true"), .Bits(16), .Addr_Bits(16)) rom_1 (
    .A(pcintr_1_p8), .sel(1'b1), .D({rom_1_d_3, rom_1_d_2, rom_1_d}));
  // PCintr pcintr_1: pin names not known; wires that end beside it: A, C, abs, intr_t, RetI, pcintr_1_p6, pcintr_1_p7, pcintr_1_p8
  assign D = stPC ? pcintr_1_p7 : 16'bz;  // Driver driver_1
  // Register register_1: pin names not known; wires that end beside it: D, C, rom_1_d, rom_1_d_2, WE, register_1_p6, register_1_p7
  // ImReg imreg_1: pin names not known; wires that end beside it: imm, iem, C, {rom_1_d_3, rom_1_d_2, rom_1_d}, imreg_1_p5
  // Control control_1: pin names not known; wires that end beside it: RetI, ioR, ioW, ld, st, br, sf, aluOp, alu2D, muxA, src2D, muxB, abs, iem, imm, WE, rom_1_d_3, stPC
  // SignExt signext_1: pin names not known; wires that end beside it: {rom_1_d_3, rom_1_d_2, rom_1_d}, signext_1_p2, signext_1_p3, signext_1_p4
  assign D = src2D ? register_1_p7 : 16'bz;  // Driver driver_2
  Multiplexer #(.Bits(16)) multiplexer_1 (
    .sel(muxA), .in_0(register_1_p6), .in_1(register_1_p7), .out(multiplexer_1_out));
  Multiplexer #(.Selector_Bits(3), .Bits(16)) multiplexer_2 (
    .sel(muxB), .in_0(register_1_p7), .in_1({16{1'b0}}), .in_2(imreg_1_p5), .in_3({16{1'b0}}),
    .in_4({16{1'b0}}), .in_5(signext_1_p2), .in_6(signext_1_p3), .in_7(signext_1_p4), .out(multiplexer_2_out));
  // Branch branch_1: pin names not known; wires that end beside it: pcintr_1_p6, br, branch_1_p3, branch_1_p4, branch_1_p5, branch_1_p3, branch_1_p4, branch_1_p5
  // ALU alu_1: pin names not known; wires that end beside it: multiplexer_1_out, aluOp, multiplexer_2_out, branch_1_p3, A, alu_1_p6, alu_1_p7, alu_1_p8
  Interrupt interrupt_1 (.nie(flagsrw_1_p1), .C(C), .imm(imm), .reti(RetI), .intr(intr), .iEn(intr_t));
  assign D = alu2D ? A : 16'bz;  // Driver driver_3
  // FlagsRW flagsrw_1: pin names not known; wires that end beside it: flagsrw_1_p1, D, ioW, ioR, A, sf, C, alu_1_p8, alu_1_p7, alu_1_p6
  RAMSinglePort #(.AddrBits(16), .Bits(16), .Addr_Bits(16)) ramsingleport_1 (.A(A), .str(st), .C(C), .ld(ld), .D(D));

  // Notes on the sheet:
  //   C: Hz: 2147483647
  //   contents of rom_1 (hex, n*v repeats v):
  //   3d12,0,ffff,31e0,4200,fffe,31e0,10e2,801e,4100,801f,3e00,ce2,fffe,320e,3f00,ffff,
  //   320e,4500,a01,8015,3e00,2400,38fc,8000,901,8015,3e00,2500,38fc,3df4
endmodule
