// Digital circuit Interrupt.dig as structural Verilog
// Simple interrupt controller.
// If an interrupt is triggered, the controller is disabled: no 
// further interrupts can be triggered. Setting the input reti 
// releases the interrupt controller.
// {{de Einfacher Interrupt-Controller.
// Wird ein Interrupt ausgelöst, wird der Controller
// gesperrt: Es können keine weiteren Interrupts
// ausgelöst werden. Erst der Eingang reti gibt den 
// Interrupt-Controller wieder frei.}}
module Interrupt (
  input  nie,
  input  C,
  input  imm,
  input  reti,
  input  intr,
  output iEn
);

  wire intLock_d, intr_d;

  RS intLock (.S(iEn), .nC(C), .R(reti), .D(intLock_d));
  RS u_intr (.S(intr), .nC(C), .R(reti), .D(intr_d));
  and and_1 (iEn, ~intLock_d, ~imm, intr_d, ~nie);  // And

  // Notes on the sheet:
  //   iEn: interrupt trigger used by the PC
  //   {{de Interrupt-Freigabe für PC}}
  //   imm: immediate register:
  //   If set, an interrupt is blocked.
  //   {{de Immediate Register:
  //   Wenn gesetzt, wird Interrupt verhindert.}}
  //   reti: return from interrupt. This signal is used to 
  //   release the interrupt controller.
  //   {{de return from interrupt. Über dieses Signal werden
  //   die Interrupts wieder freigegeben.}}
  //   intr: interrupt trigger {{de Interrupt Anforderung}}
endmodule
